# Fritzing sketch binary-clock-new (saved by Fritzing 0.9.2b)
breadboards: 1

parts:
  Power_plug1 = Power plug
  U1 = Voltage Regulator - 5V [package="TO220 [THT]"]
  C1 = Tantalum Capacitor [capacitance=10µF package="100 mil [THT, tantalum]"]
  C2 = Tantalum Capacitor [capacitance=10µF package="100 mil [THT, tantalum]"]
  U2 = atmega328 [package=dip]
  D1 = Rectifier Diode [part_number=1N4001 package="300 mil [THT]"]
  D2 = Rectifier Diode [part_number=1N4001 package="300 mil [THT]"]
  XTAL1 = Crystal [frequency="16 Mhz" package=THT]
  C3 = Ceramic Capacitor [capacitance=22pF package="100 mil [THT, multilayer]"]
  C4 = Ceramic Capacitor [capacitance=22pF package="100 mil [THT, multilayer]"]
  R1 = Resistor [tolerance=±5% resistance=10k package=THT]
  R2 = Resistor [tolerance=±5% resistance=10k package=THT]
  R3 = Resistor [tolerance=±5% resistance=10k package=THT]
  S1 = Pushbutton [package=THT]
  S2 = Pushbutton [package=THT]
  S3 = Pushbutton [package=THT]
  LED1 = LED - 5mm [color="White (8000K)" current=20mA package="5 mm [THT]"]
  R4 = Resistor [tolerance=±5% resistance=220 package=THT]
  R5 = Resistor [tolerance=±5% resistance=220 package=THT]
  R6 = Resistor [tolerance=±5% resistance=220 package=THT]
  R7 = Resistor [tolerance=±5% resistance=220 package=THT]
  R8 = Resistor [tolerance=±5% resistance=220 package=THT]
  R9 = Resistor [tolerance=±5% resistance=220 package=THT]
  R10 = Resistor [tolerance=±5% resistance=220 package=THT]
  R11 = Resistor [tolerance=±5% resistance=220 package=THT]
  R12 = Resistor [tolerance=±5% resistance=220 package=THT]
  R13 = Resistor [tolerance=±5% resistance=220 package=THT]
  R14 = Resistor [tolerance=±5% resistance=220 package=THT]
  R15 = Resistor [tolerance=±5% resistance=220 package=THT]
  R16 = Resistor [tolerance=±5% resistance=220 package=THT]
  U3 = 74HC595 [package="DIP16 [THT]"]
  U4 = 74HC595 [package="DIP16 [THT]"]
  RTC = IC, DIP package, 4 pins [chip_label=RTC]
  C5 = Ceramic Capacitor [capacitance=100nF package="100 mil [THT, multilayer]"]
  C6 = Ceramic Capacitor [capacitance=100nF package="100 mil [THT, multilayer]"]
  C7 = Ceramic Capacitor [capacitance=100nF package="100 mil [THT, multilayer]"]
  C8 = Ceramic Capacitor [capacitance=100nF package="100 mil [THT, multilayer]"]
  R17 = Rotary Potentiometer (Small) [maximum_resistance=10kΩ package=THT]
  Q1 = NPN-Transistor [package="TO92 [THT]"]
  R18 = Resistor [tolerance=±5% resistance=1k package=THT]
  LED14 = LED - 5mm [color="White (8000K)" current=20mA package="5 mm [THT]"]
  LED15 = LED - 5mm [color="White (8000K)" current=20mA package="5 mm [THT]"]
  LED16 = LED - 5mm [color="White (8000K)" current=20mA package="5 mm [THT]"]
  LED17 = LED - 5mm [color="White (8000K)" current=20mA package="5 mm [THT]"]
  LED18 = LED - 5mm [color="White (8000K)" current=20mA package="5 mm [THT]"]
  LED19 = LED - 5mm [color="White (8000K)" current=20mA package="5 mm [THT]"]
  LED20 = LED - 5mm [color="White (8000K)" current=20mA package="5 mm [THT]"]
  LED21 = LED - 5mm [color="White (8000K)" current=20mA package="5 mm [THT]"]
  LED22 = LED - 5mm [color="White (8000K)" current=20mA package="5 mm [THT]"]
  LED23 = LED - 5mm [color="White (8000K)" current=20mA package="5 mm [THT]"]
  LED24 = LED - 5mm [color="White (8000K)" current=20mA package="5 mm [THT]"]
  LED25 = LED - 5mm [color="White (8000K)" current=20mA package="5 mm [THT]"]

nets:
  N1: Power_plug1.VCC, D1.anode
  N2: Power_plug1.GND, D2.cathode
  12v: U1.input_voltage, C2.+, D1.cathode
  GND: U1.GND, C1.-, C2.-, U2.GND, D2.anode, C3.0, C4.0, R2.Pin_1, R3.Pin_1, S1.leg1, U3.GND, U3.OE, U4.GND, U4.OE, RTC.pin2, C5.1, C6.0, C7.0, C8.0, R17.leg2, Q1.E
  5v: U1.output_voltage, C1.+, U2.VCC, U2.AVCC, U2.AREF, R1.Pin_1, S2.leg1, S3.leg1, U3.MR, U3.VCC, U4.MR, U4.VCC, RTC.pin1, C5.0, C6.1, C7.1, C8.1, R17.leg1
  N3: U2.RESET, R1.Pin_0, S1.leg0
  N4: U2.XLAT1, XTAL1.pin_0, C3.1
  N5: U2.XLAT2, XTAL1.pin_1, C4.1
  N6: U2.D7, R2.Pin_0, S3.leg0
  N7: U2.D8, R3.Pin_0, S2.leg0
  sr_clk: U2.D9_(PWM), U3.SH_CP, U4.SH_CP
  sr_latch: U2.D10_(PWM), U3.ST_CP, U4.ST_CP
  sr_data: U2.D11_(PWM), U4.DS
  N8: U2.A1, R18.Pin_0
  N9: U2.A3, R17.wiper
  sda: U2.A4, RTC.pin4
  scl: U2.A5, RTC.pin3
  N10: LED1.cathode, R4.Pin_1
  N11: LED1.anode, U4.Q2
  led_sink: R4.Pin_0, R5.Pin_0, R6.Pin_0, R7.Pin_0, R8.Pin_0, R9.Pin_0, R10.Pin_0, R11.Pin_0, R12.Pin_0, R13.Pin_0, R14.Pin_0, R15.Pin_0, R16.Pin_0, Q1.C
  N12: R5.Pin_1, LED14.cathode
  N13: R6.Pin_1, LED15.cathode
  N14: R7.Pin_1, LED17.cathode
  N15: R8.Pin_1, LED16.cathode
  N16: R9.Pin_1, LED19.cathode
  N17: R10.Pin_1, LED18.cathode
  N18: R11.Pin_1, LED21.cathode
  N19: R12.Pin_1, LED20.cathode
  N20: R13.Pin_1, LED22.cathode
  N21: R14.Pin_1, LED24.cathode
  N22: R15.Pin_1, LED25.cathode
  N23: R16.Pin_1, LED23.cathode
  N24: U3.Q1, LED19.anode
  N25: U3.Q2, LED20.anode
  N26: U3.Q3, LED21.anode
  N27: U3.Q4, LED22.anode
  N28: U3.Q5, LED23.anode
  N29: U3.Q6, LED24.anode
  N30: U3.Q7, LED25.anode
  sr_data_output: U3.DS, U4.Q7'
  N31: U4.Q3, LED14.anode
  N32: U4.Q4, LED15.anode
  N33: U4.Q5, LED16.anode
  N34: U4.Q6, LED17.anode
  N35: U4.Q7, LED18.anode
  N36: Q1.B, R18.Pin_1

notes:
  FD
  SD
  TD
